// Logisim project CPU.circ as structural Verilog: 1 circuit, main circuit main
module main (
  input  Reset
);

  wire alu_1_eq, and_1_out, clock_1_out, controller_1_p3, controller_1_p5, controller_1_p6, controller_1_p7,
       controller_1_p8, controller_1_p11, controller_1_p12;
  wire [1:0] controller_1_p4, controller_1_p9;
  wire [4:0] controller_1_p10, multiplexer_1_out;
  wire [31:0] alu_1_s, dm_1_output, ext_1_out_3, grf_1_out_8, grf_1_out_9, ifu_1_instruction,
       multiplexer_2_out, multiplexer_3_out, shifter_1_out;

  Clock clock_1 (.out(clock_1_out));
  // Probe on ifu_1_instruction
  IFU ifu_1 (.Clock(clock_1_out), .Reset(Reset), .Instruction(ifu_1_instruction));
  EXT ext_1 (.Src(ifu_1_instruction[15:0]), .Signed(controller_1_p8), .out_3(ext_1_out_3));
  Shifter #(.width(32)) shifter_1 (.in(ext_1_out_3), .\dist (controller_1_p10), .out(shifter_1_out));
  Multiplexer #(.width(5), .enable("false")) multiplexer_1 (
    .in0(ifu_1_instruction[15:11]), .in1(ifu_1_instruction[20:16]), .out(multiplexer_1_out),
    .sel(controller_1_p12));
  // Controller controller_1: pin names not known; wires that end beside it: ifu_1_instruction[31:26], ifu_1_instruction[5:0], controller_1_p3, controller_1_p4, controller_1_p5, controller_1_p6, controller_1_p7, controller_1_p8, controller_1_p9, controller_1_p10, controller_1_p11, controller_1_p12
  Multiplexer #(.select(2), .width(32), .enable("false")) multiplexer_2 (
    .in0(alu_1_s), .in1(shifter_1_out), .in2(dm_1_output), .out(multiplexer_2_out), .sel(controller_1_p4));  // open: in3
  GRF grf_1 (
    .Input(multiplexer_2_out), .read_addr0(ifu_1_instruction[25:21]), .read_addr1(ifu_1_instruction[20:16]),
    .write_enable(controller_1_p3), .write_addr(multiplexer_1_out), .Clock(clock_1_out), .Reset(Reset),
    .out_8(grf_1_out_8), .out_9(grf_1_out_9));
  Multiplexer #(.width(32), .enable("false")) multiplexer_3 (
    .in0(grf_1_out_9), .in1(shifter_1_out), .out(multiplexer_3_out), .sel(controller_1_p7));
  ALU alu_1 (
    .A(grf_1_out_8), .B(multiplexer_3_out), .Control(controller_1_p9), .S(alu_1_s), .eq(alu_1_eq));  // open: lt, gt
  and and_1 (and_1_out, controller_1_p11, alu_1_eq);
  DM dm_1 (
    .Addr(alu_1_s[6:2]), .Data(grf_1_out_9), .S(controller_1_p6), .Clock(clock_1_out), .L(controller_1_p5),
    .C(Reset), .Output(dm_1_output));
endmodule
