// Logisim project Controller.circ as structural Verilog: 6 circuits, main circuit Controller
module Controller (
  input  [5:0] Op,
  input  [5:0] Func,
  input  [4:0] extra,
  output GRF_write,
  output [1:0] GRF_select,
  output Memory_read,
  output Memory_write,
  output ALU_select,
  output EXT_signed,
  output [1:0] ALU_main,
  output [4:0] EXT_width,
  output beq,
  output GRF_writeAddrSelect
);

  wire andlogic_1_p3, andlogic_1_p4, andlogic_1_p5, andlogic_1_p6, andlogic_1_p7, andlogic_1_p8,
       andlogic_1_p9, andlogic_1_p10;

  // AndLogic andlogic_1: pin names not known; wires that end beside it: Op, Func, andlogic_1_p3, andlogic_1_p4, andlogic_1_p5, andlogic_1_p6, andlogic_1_p7, andlogic_1_p8, andlogic_1_p9, andlogic_1_p10
  OrLogic orlogic_1 (
    .div(andlogic_1_p3), .divu(andlogic_1_p4), .jalr(andlogic_1_p5), .jr(andlogic_1_p6),
    .mfhi(andlogic_1_p7), .mflo(andlogic_1_p8), .mthi(andlogic_1_p9), .mtlo(andlogic_1_p10),
    .GRF_write(GRF_write), .GRF_select(GRF_select), .Memory_read(Memory_read), .Memory_write(Memory_write),
    .ALU_select(ALU_select), .EXT_signed(EXT_signed), .ALU_main(ALU_main), .Shifter_width(EXT_width),
    .beq_2(beq), .GRF_writeAddrSelect(GRF_writeAddrSelect));  // open: addi, addiu, andi, beq, bgtz, blez, bne, j, jal, lui, lw, ori, slti, sltiu, sw, xori, add, addu, and, mult, multu, nor, or, sll, sllv, slt, sltu, sra, srav, srl, srlv, sub, subu, xor, bgez, bgezal, bltz, bltzal

  // Notes on the sheet:
  //   EXT_width: pull=down
endmodule

module AndLogic (
  input  [5:0] OperationCode,
  input  [5:0] Function,
  input  [4:0] extra,
  output addi,
  output addiu,
  output andi,
  output beq,
  output bgtz,
  output blez,
  output bne,
  output j,
  output jal,
  output lui,
  output lw,
  output ori,
  output slti,
  output sltiu,
  output sw,
  output xori,
  output add,
  output addu,
  output \and ,
  output div,
  output divu,
  output jalr,
  output jr,
  output mfhi,
  output mflo,
  output mthi,
  output mtlo,
  output mult,
  output multu,
  output \nor ,
  output \or ,
  output sll,
  output sllv,
  output slt,
  output sltu,
  output sra,
  output srav,
  output srl,
  output srlv,
  output sub,
  output subu,
  output \xor ,
  output bgez,
  output bgezal,
  output bltz,
  output bltzal
);

  wire andlogic_operationcodedetector_1_extra, andlogic_operationcodedetector_1_special;

  AndLogic__OperationCodeDetector andlogic_operationcodedetector_1 (
    .opcode(OperationCode), .special(andlogic_operationcodedetector_1_special),
    .extra(andlogic_operationcodedetector_1_extra), .addi(addi), .addiu(addiu), .andi(andi), .beq(beq),
    .bgtz(bgtz), .blez(blez), .bne(bne), .j(j), .jal(jal), .lui(lui), .lw(lw), .ori(ori), .slti(slti),
    .sltiu(sltiu), .sw(sw), .xori(xori));
  AddLogic__FuncrionDetector addlogic_funcriondetector_1 (
    .funct(Function), .special(andlogic_operationcodedetector_1_special), .add(add), .addu(addu),
    .\and (\and ), .div(div), .divu(divu), .jalr(jalr), .jr(jr), .mfhi(mfhi), .mflo(mflo), .mthi(mthi),
    .mtlo(mtlo), .mult(mult), .multu(multu), .\nor (\nor ), .\or (\or ), .sll(sll), .sllv(sllv), .slt(slt),
    .sltu(sltu), .sra(sra), .srav(srav), .srl(srl), .srlv(srlv), .sub(sub), .subu(subu), .\xor (\xor ));
  AndLogic__extra andlogic_extra_1 (
    .extra(extra), .is_extra(andlogic_operationcodedetector_1_extra), .bgez(bgez), .bgezal(bgezal),
    .bltz(bltz), .bltzal(bltzal));
endmodule

module AndLogic__OperationCodeDetector (
  input  [5:0] opcode,
  output addi,
  output addiu,
  output andi,
  output beq,
  output bgtz,
  output blez,
  output bne,
  output j,
  output jal,
  output lui,
  output lw,
  output ori,
  output slti,
  output sltiu,
  output sw,
  output xori,
  output special,
  output extra
);

  wire not_1_out, not_2_out, not_3_out, not_4_out, not_5_out, not_6_out;

  not not_1 (not_1_out, opcode[2]);
  not not_2 (not_2_out, opcode[1]);
  not not_3 (not_3_out, opcode[0]);
  not not_4 (not_4_out, opcode[3]);
  not not_5 (not_5_out, opcode[5]);
  not not_6 (not_6_out, opcode[4]);
  and and_1 (addi, not_3_out, not_2_out, not_1_out, opcode[3], not_6_out, not_5_out);
  and and_2 (addiu, opcode[0], not_2_out, not_1_out, opcode[3], not_6_out, not_5_out);
  and and_3 (andi, not_3_out, not_2_out, opcode[2], opcode[3], not_6_out, not_5_out);
  and and_4 (beq, not_3_out, not_2_out, opcode[2], not_4_out, not_6_out, not_5_out);
  and and_5 (bgtz, opcode[0], opcode[1], opcode[2], not_4_out, not_6_out, not_5_out);
  and and_6 (blez, not_3_out, opcode[1], opcode[2], not_4_out, not_6_out, not_5_out);
  and and_7 (bne, opcode[0], not_2_out, opcode[2], not_4_out, not_6_out, not_5_out);
  and and_8 (j, not_3_out, opcode[1], not_1_out, not_4_out, not_6_out, not_5_out);
  and and_9 (jal, opcode[0], opcode[1], not_1_out, not_4_out, not_6_out, not_5_out);
  and and_10 (lui, opcode[0], opcode[1], opcode[2], opcode[3], not_6_out, not_5_out);
  and and_11 (lw, opcode[0], opcode[1], not_1_out, not_4_out, not_6_out, opcode[5]);
  and and_12 (ori, opcode[0], not_2_out, opcode[2], opcode[3], not_6_out, not_5_out);
  and and_13 (slti, not_3_out, opcode[1], not_1_out, opcode[3], not_6_out, not_5_out);
  and and_14 (sltiu, opcode[0], opcode[1], not_1_out, opcode[3], not_6_out, not_5_out);
  and and_15 (sw, opcode[0], opcode[1], not_1_out, opcode[3], not_6_out, opcode[5]);
  and and_16 (xori, not_3_out, opcode[1], opcode[2], opcode[3], not_6_out, not_5_out);
  and and_17 (special, not_3_out, not_2_out, not_1_out, not_4_out, not_6_out, not_5_out);
  and and_18 (extra, opcode[0], not_2_out, not_1_out, not_4_out, not_6_out, not_5_out);
endmodule

module AddLogic__FuncrionDetector (
  input  special,
  input  [5:0] funct,
  output add,
  output addu,
  output \and ,
  output div,
  output divu,
  output jalr,
  output jr,
  output mfhi,
  output mflo,
  output mthi,
  output mtlo,
  output mult,
  output multu,
  output \nor ,
  output \or ,
  output sll,
  output sllv,
  output slt,
  output sltu,
  output sra,
  output srav,
  output srl,
  output srlv,
  output sub,
  output subu,
  output \xor 
);

  wire not_1_out, not_2_out, not_3_out, not_4_out, not_5_out, not_6_out;

  not not_1 (not_1_out, funct[2]);
  not not_2 (not_2_out, funct[1]);
  not not_3 (not_3_out, funct[0]);
  not not_4 (not_4_out, funct[4]);
  not not_5 (not_5_out, funct[3]);
  not not_6 (not_6_out, funct[5]);
  and and_1 (add, special, not_3_out, not_2_out, not_1_out, not_5_out, not_4_out, funct[5]);
  and and_2 (addu, special, funct[0], not_2_out, not_1_out, not_5_out, not_4_out, funct[5]);
  and and_3 (\and , special, not_3_out, not_2_out, funct[2], not_5_out, not_4_out, funct[5]);
  and and_4 (div, special, not_3_out, funct[1], not_1_out, funct[3], funct[4], not_6_out);
  and and_5 (divu, special, funct[0], funct[1], not_1_out, funct[3], funct[4], not_6_out);
  and and_6 (jalr, special, funct[0], not_2_out, not_1_out, funct[3], not_4_out, not_6_out);
  and and_7 (jr, special, not_3_out, not_2_out, not_1_out, funct[3], not_4_out, not_6_out);
  and and_8 (mfhi, special, not_3_out, not_2_out, not_1_out, not_5_out, funct[4], not_6_out);
  and and_9 (mflo, special, not_3_out, funct[1], not_1_out, not_5_out, funct[4], not_6_out);
  and and_10 (mthi, special, funct[0], not_2_out, not_1_out, not_5_out, funct[4], not_6_out);
  and and_11 (mtlo, special, funct[0], funct[1], not_1_out, not_5_out, funct[4], not_6_out);
  and and_12 (mult, special, not_3_out, not_2_out, not_1_out, funct[3], funct[4], not_6_out);
  and and_13 (multu, special, funct[0], not_2_out, not_1_out, funct[3], funct[4], not_6_out);
  and and_14 (\nor , special, funct[0], funct[1], funct[2], not_5_out, not_4_out, funct[5]);
  and and_15 (\or , special, funct[0], not_2_out, funct[2], not_5_out, not_4_out, funct[5]);
  and and_16 (sll, special, not_3_out, not_2_out, not_1_out, not_5_out, not_4_out, not_6_out);
  and and_17 (sllv, special, not_3_out, not_2_out, funct[2], not_5_out, not_4_out, not_6_out);
  and and_18 (slt, special, not_3_out, funct[1], not_1_out, funct[3], not_4_out, funct[5]);
  and and_19 (sltu, special, funct[0], funct[1], not_1_out, funct[3], not_4_out, funct[5]);
  and and_20 (sra, special, funct[0], funct[1], not_1_out, not_5_out, not_4_out, not_6_out);
  and and_21 (srav, special, funct[0], funct[1], funct[2], not_5_out, not_4_out, not_6_out);
  and and_22 (srl, special, not_3_out, funct[1], not_1_out, not_5_out, not_4_out, not_6_out);
  and and_23 (srlv, special, not_3_out, funct[1], funct[2], not_5_out, not_4_out, not_6_out);
  and and_24 (sub, special, not_3_out, funct[1], not_1_out, not_5_out, not_4_out, funct[5]);
  and and_25 (subu, special, funct[0], funct[1], not_1_out, not_5_out, not_4_out, funct[5]);
  and and_26 (\xor , special, not_3_out, funct[1], funct[2], not_5_out, not_4_out, funct[5]);
endmodule

module OrLogic (
  input  addi,
  input  addiu,
  input  andi,
  input  beq,
  input  bgtz,
  input  blez,
  input  bne,
  input  j,
  input  jal,
  input  lui,
  input  lw,
  input  ori,
  input  slti,
  input  sltiu,
  input  sw,
  input  xori,
  input  add,
  input  addu,
  input  \and ,
  input  div,
  input  divu,
  input  jalr,
  input  jr,
  input  mfhi,
  input  mflo,
  input  mthi,
  input  mtlo,
  input  mult,
  input  multu,
  input  \nor ,
  input  \or ,
  input  sll,
  input  sllv,
  input  slt,
  input  sltu,
  input  sra,
  input  srav,
  input  srl,
  input  srlv,
  input  sub,
  input  subu,
  input  \xor ,
  input  bgez,
  input  bgezal,
  input  bltz,
  input  bltzal,
  output GRF_write,
  output [1:0] GRF_select,
  output Memory_read,
  output Memory_write,
  output ALU_select,
  output EXT_signed,
  output [1:0] ALU_main,
  output [4:0] Shifter_width,
  output beq_2,
  output GRF_writeAddrSelect
);

  wire addu_t, lui_t, lw_t, ori_t, subu_t, sw_t;

  or or_1 (GRF_write, addu_t, subu_t, ori_t, lw_t, lui_t);
  buf or_2 (GRF_select[0], lui_t);  // OR_Gate
  buf or_3 (GRF_select[1], lw_t);  // OR_Gate
  buf or_4 (Memory_read, lw_t);  // OR_Gate
  buf or_5 (Memory_write, sw_t);  // OR_Gate
  or or_6 (ALU_select, ori_t, lw_t, sw_t);
  or or_7 (EXT_signed, lw_t, sw_t, beq_2, lui_t);
  or or_8 (ALU_main[0], subu_t, beq_2);
  buf or_9 (ALU_main[1], ori_t);  // OR_Gate
  buf or_10 (Shifter_width[1], beq_2);  // OR_Gate
  buf or_11 (Shifter_width[4], lui_t);  // OR_Gate
  or or_12 (GRF_writeAddrSelect, ori_t, lw_t, lui_t);

  assign {Shifter_width[3:2], Shifter_width[0]} = 3'b000;

  // Other names for the same wires on the sheet: beq_t = beq_2

  // Notes on the sheet:
  //   Shifter_width: pull=down
endmodule

module AndLogic__extra (
  input  is_extra,
  input  [4:0] extra,
  output bgez,
  output bgezal,
  output bltz,
  output bltzal
);

  wire and_1_out, and_2_out, and_3_out, and_4_out, not_1_out, not_2_out, not_3_out, not_4_out, not_5_out;

  not not_1 (not_1_out, extra[1]);
  not not_2 (not_2_out, extra[0]);
  not not_3 (not_3_out, extra[3]);
  not not_4 (not_4_out, extra[4]);
  not not_5 (not_5_out, extra[2]);
  and and_1 (and_1_out, extra[0], not_1_out, not_5_out, not_3_out, not_4_out);
  and and_2 (and_2_out, extra[0], not_1_out, not_5_out, not_3_out, extra[4]);
  and and_3 (and_3_out, not_2_out, not_1_out, not_5_out, not_3_out, not_4_out);
  and and_4 (and_4_out, not_2_out, not_1_out, not_5_out, not_3_out, extra[4]);
  and and_5 (bgez, is_extra, and_1_out);
  and and_6 (bgezal, is_extra, and_2_out);
  and and_7 (bltz, is_extra, and_3_out);
  and and_8 (bltzal, is_extra, and_4_out);
endmodule
