// Logisim project IFU.circ as structural Verilog: 1 circuit, main circuit IFU
module IFU (
  input  [1:0] PC_select,
  input  Clock,
  input  Reset,
  input  [31:0] \input ,
  output [31:0] Instruction,
  output [31:0] PC_4
);

  wire [31:0] multiplexer_1_out, n32_bit_adder_1_s, n32_bit_adder_3_s, PC_q;

  _32_bit_adder u_32_bit_adder_1 (.A(\input ), .B(32'hffffd000), .S(n32_bit_adder_1_s));  // open: Cin, Cout
  Multiplexer #(.select(2), .width(32), .enable("false")) multiplexer_1 (
    .in0(PC_4), .in1(n32_bit_adder_3_s), .in2(n32_bit_adder_1_s), .out(multiplexer_1_out), .sel(PC_select));  // open: in3
  Register #(.width(32)) PC (.D(multiplexer_1_out), .Q(PC_q), .clk(Clock), .clr(Reset));  // open: en
  _32_bit_adder u_32_bit_adder_2 (.A(PC_q), .B(32'h4), .S(PC_4));  // open: Cin, Cout
  _32_bit_adder u_32_bit_adder_3 (.A(PC_4), .B(\input ), .S(n32_bit_adder_3_s));  // open: Cin, Cout
  ROM #(.addrWidth(5), .dataWidth(32)) rom_1 (.addr(PC_q[6:2]), .data(Instruction));  // open: sel
endmodule
