// Logisim project SRF.circ as structural Verilog: 1 circuit, main circuit SRF
module SRF (
  input  [31:0] in_1,
  input  [31:0] in_2,
  output [31:0] HI,
  output [31:0] LO
);

  wire [31:0] multiplier_1_cout, multiplier_1_out;

  // Probe on multiplier_1_out
  Multiplier #(.width(32)) multiplier_1 (
    .a(in_1), .b(in_2), .out(multiplier_1_out), .cout(multiplier_1_cout));  // open: cin
  // Probe on multiplier_1_cout
  Divider #(.width(32)) divider_1 ();  // open: a, b, out, upper, rem
  Register #(.width(32)) u_HI (.Q(HI));  // open: D, en, clk, clr
  Register #(.width(32)) u_LO (.Q(LO));  // open: D, en, clk, clr
endmodule
